# Fritzing sketch Circuito_no fritzzing (saved by Fritzing 0.9.3b)

parts:
  Componente1 = Arduino Uno (Rev3)
  C1 = Electrolytic Capacitor [capacitance=1µF package="100 mil [THT, electrolytic]"]
  R1 = Trimmer Potentiometer [maximum_resistance=10kΩ package=THT]
  R2 = Photocell (LDR) [package=THT]
  Q1 = Basic FET P-Channel [package="TO220 [THT]"]
  SPKR1 = Loudspeaker
  K1 = Relay [part_number=FRS1B-S package=THT]
  Q3 = NPN-Transistor [package="SOT-23 [SMD]"]
  S1 = Toggle Switch [package=THT]
  R3 = Resistor [tolerance=±5% resistance=220 package=THT]
  R4 = Resistor [tolerance=±5% resistance=220 package=THT]  # not connected
  R5 = Resistor [tolerance=±5% resistance=220 package=THT]  # not connected
  LED1 = LED - 5mm [color="Red (633nm)" package="5 mm [THT]"]  # not connected
  LED2 = LED - 5mm [color="Red (633nm)" package="5 mm [THT]"]  # not connected
  VCC1 = Battery
  R6 = Resistor [tolerance=±5% resistance=220 package=THT]
  R7 = Resistor [tolerance=±5% resistance=220 package=THT]

nets:
  N1: Componente1.A0, R2.pin_1
  N2: Componente1.A1, R1.wiper
  N3: Componente1.D10_PWM/SS, S1.L1, R3.Pin_1
  N4: Componente1.D11_PWM/MOSI, R6.Pin_0
  N5: Componente1.D12/MISO, R7.Pin_0
  N6: Componente1.5V, C1.+, R2.pin_0, K1.COIL2, S1.COM
  N7: Componente1.GND, Q1.drain
  N8: R1.leg2, SPKR1.pin1, R3.Pin_0
  N9: SPKR1.pin2, K1.C1, K1.C2
  N10: K1.COIL1, Q3.2
  N11: K1.B, VCC1.+

notes:
  7805
  Bc548
